# Fritzing sketch Fritzing_Schematics (saved by Fritzing 0.9.4)
breadboards: 1

parts:
  Part1 = Arduino Uno (Rev3) - ICSP
  DHT1 = Humidity and Temperature Sensor DHT11
  OLED_I2C1 = OLED 128x64 I2C Monochrome Display
  R1 = Resistor [tolerance=±5% resistance=220 package="2010 [SMD]"]

nets:
  N1: Part1.A4/SDA, OLED_I2C1.SDA
  N2: Part1.A5/SCL, OLED_I2C1.SCK
  N3: Part1.D2, DHT1.Data-signal, R1.Pin_0
  5V: Part1.5V, DHT1.Vcc, OLED_I2C1.VDD, R1.Pin_1
  N4: DHT1.GND_2, OLED_I2C1.GND

custom parts:
  Humidity and Temperature Sensor DHT11: Digital relative humidity & temperature sensor DHT11
